# Fritzing sketch Arduino Weather Station1 (saved by Fritzing 0.9.3b)
circuit board: 8.46667cm x 5.64444cm
breadboards: 3

parts:
  Part1 = Arduino Uno (Rev3) - ICSP
  U3 = LM393 [package=so08]
  Part3 = Barometric Pressure Sensor - BMP085 Breakout
  RHT1 = Humidity and Temperature Sensor RHT03
  Part5 = SparkFun ESP8266 Thing
  LED1 = smd LED [color="Red (633nm)" package="0603 [SMD]"]
  R1 = Resistor [tolerance=±5% resistance=220 package="0603 [SMD]"]
  LED2 = smd LED [color="Red (633nm)" package="0603 [SMD]"]
  R2 = Resistor [tolerance=±5% resistance=220 package="0603 [SMD]"]
  LED3 = smd LED [color="Red (633nm)" package="0603 [SMD]"]
  R3 = Resistor [tolerance=±5% resistance=220 package="0603 [SMD]"]
  LED4 = smd LED [color="Red (633nm)" package="0603 [SMD]"]
  R4 = Resistor [tolerance=±5% resistance=220 package="0603 [SMD]"]
  LED5 = smd LED [color="Red (633nm)" package="0603 [SMD]"]
  R5 = Resistor [tolerance=±5% resistance=220 package="0805 [SMD]"]
  U4 = LM393 [package=so08]
  LED6 = smd LED [color="Red (633nm)" package="0603 [SMD]"]
  R6 = Resistor [tolerance=±5% resistance=220 package="0805 [SMD]"]
  LED7 = smd LED [color="Red (633nm)" package="0603 [SMD]"]
  R7 = Resistor [tolerance=±5% resistance=220 package="0603 [SMD]"]
  LED8 = smd LED [color="Red (633nm)" package="0603 [SMD]"]
  R8 = Resistor [tolerance=±5% resistance=220 package="0603 [SMD]"]
  VCC1 = Battery block 9V
  R9 = Resistor [tolerance=±5% resistance=220 package=THT]
  R10 = Resistor [tolerance=±5% resistance=220 package=THT]
  S1 = Pushbutton [package="[SMD]"]

nets:
  N1: Part1.A1, R9.Pin_0, R10.Pin_1
  N2: Part1.A2, U3.G1_OUT
  N3: Part1.A3, U4.G1_OUT
  N4: Part1.A4/SDA, Part3.SDA
  N5: Part1.A5/SCL, Part3.SCL
  5V: Part1.5V, Part1.D7, U3.G1_V+, RHT1.Vcc, U4.G1_V+, S1.Pin_1, S1.Pin_2, S1.Pin_3, S1.Pin_4
  GND: Part1.GND, U3.G1_V-, Part3.GND, RHT1.GND_2, Part5.GND, LED3.cathode, LED5.anode, U4.G1_V-, LED6.anode, R10.Pin_0
  N6: Part1.D10_PWM/SS, R5.Pin_0
  N7: Part1.D11_PWM/MOSI, R6.Pin_0
  N8: Part1.D12/MISO, R7.Pin_1
  N9: Part1.D13/SCK, R8.Pin_0
  N10: Part1.D0/RX, Part5.U0RXI
  N11: Part1.D1/TX, Part5.U0TXO
  N12: Part1.D2, RHT1.Data-signal
  N13: Part1.D3_PWM, R1.Pin_1
  N14: Part1.D4, R2.Pin_0
  N15: Part1.D5_PWM, R3.Pin_0
  N16: Part1.D6_PWM, R4.Pin_0
  VCC: Part1.3V3, Part3.VCC, Part5.VCC
  N17: LED1.cathode, LED2.cathode, LED4.cathode, LED7.cathode
  N18: LED1.anode, R1.Pin_0
  N19: LED2.anode, R2.Pin_1
  N20: LED3.anode, R3.Pin_1
  N21: LED4.anode, R4.Pin_1
  N22: LED5.cathode, R5.Pin_1
  N23: LED6.cathode, R6.Pin_1
  N24: LED7.anode, R7.Pin_0
  N25: LED8.anode, R8.Pin_1
  N26: VCC1.+, R9.Pin_1

notes:
  Battery Indicator LEDs
  Barometer Led
  DHT 11 Led
  Rain Drop Sensor
  Soil Mositure Sensor
